# Fritzing sketch Wiring (saved by Fritzing 0.9.3b)
circuit board: 8.46667cm x 5.64444cm
breadboards: 1

parts:
  Onderdeel1 = Arduino Uno (Rev3)
  LCM1602_IIC1 = LCM1602 IIC [part_number="LCM1602 IIC" chip_label="LCM1602 IIC" package="DIP (Dual Inline) [THT]"]
  LCD1 = LCD screen
  DHT1 = DHT11 Humitidy and Temperature Sensor

nets:
  N1: Onderdeel1.A4/SDA, LCM1602_IIC1.SDA
  N2: Onderdeel1.A5/SCL, LCM1602_IIC1.SCL
  N3: Onderdeel1.D7, DHT1.DATA
  5V: Onderdeel1.5V, LCM1602_IIC1.VCC, DHT1.VDD
  GND: Onderdeel1.GND, LCM1602_IIC1.GND, DHT1.GND
  VSS: LCM1602_IIC1.VSS, LCD1.VSS
  VDD: LCM1602_IIC1.VDD, LCD1.VDD
  N4: LCM1602_IIC1.V0, LCD1.V0
  N5: LCM1602_IIC1.RS, LCD1.RS
  N6: LCM1602_IIC1.RW, LCD1.R/W
  N7: LCM1602_IIC1.E, LCD1.E
  N8: LCM1602_IIC1.D0, LCD1.DB0
  N9: LCM1602_IIC1.D1, LCD1.DB1
  N10: LCM1602_IIC1.D2, LCD1.DB2
  N11: LCM1602_IIC1.D3, LCD1.DB3
  N12: LCM1602_IIC1.D4, LCD1.DB4
  N13: LCM1602_IIC1.D5, LCD1.DB5
  N14: LCM1602_IIC1.D6, LCD1.DB6
  N15: LCM1602_IIC1.D7, LCD1.DB7
  N16: LCM1602_IIC1.A, LCD1.LED+
  N17: LCM1602_IIC1.K, LCD1.LED-
  N18: LCM1602_IIC1.LED_A, LCM1602_IIC1.LED_B

custom parts:
  LCM1602 IIC: I2C-Module to use a 1602 or 2004 LCD on with the wire.h libory Serial LCD Modul
  DHT11 Humitidy and Temperature Sensor: DHT11 Humidity and Temperature Sensor

// code stored in the sketch: AnalogReadSerial2LCD_LED.ino
/* YourDuino.com Example Software Sketch
 16 character 2 line I2C Display
 Backpack Interface labelled "YwRobot Arduino LCM1602 IIC V1"
 terry@yourduino.com */
 
/*-----( Import needed libraries )-----*/
#include <Wire.h>  // Comes with Arduino IDE
// Get the LCD I2C Library here: 
// https://bitbucket.org/fmalpartida/new-liquidcrystal/downloads
// Move any other LCD libraries to another folder or delete them
// See Library "Docs" folder for possible commands etc.
#include <LiquidCrystal_I2C.h>
 
/*-----( Declare Constants )-----*/
/*-----( Declare objects )-----*/
// set the LCD address to 0x27 for a 20 chars 4 line display
// Set the pins on the I2C chip used for LCD connections:
//                    addr, en,rw,rs,d4,d5,d6,d7,bl,blpol
LiquidCrystal_I2C lcd(0x27, 2, 1, 0, 4, 5, 6, 7, 3, POSITIVE);  // Set the LCD I2C address

#include <dht.h>

dht DHT;

#define DHT11_PIN 7
void setup()
{
  Serial.begin(9600);
  // initialize library
  lcd.begin(16,2);
  // blink backlight three times
  for(int i = 0; i< 3; i++)
  {
    lcd.backlight();
    delay(250);
    lcd.noBacklight();
    delay(250);
  }
  lcd.backlight();
  // set cursor to positon x=0, y=0
}
 
 
void loop()
{
    int chk = DHT.read11(DHT11_PIN);
  String temp = "Temperature = ";
  String tempval = temp +DHT.temperature;
  String hum = "Humidity = ";
  String humval = hum +DHT.humidity;
  lcd.setCursor(0,0);
  lcd.print(tempval);
  lcd.setCursor(0,1);
  lcd.print(humval);
  delay(1000);
}
